// Logisim project 4_Bit_Processor.circ as structural Verilog: 17 circuits, main circuit main
module main (
  input  Reset
);

  wire clk_tun, DWE, SUB, WE;
  wire [1:0] AFS, RSS;
  wire [2:0] Addr_B, addrA_tun, addrD_tun;
  wire [3:0] A_out, ALU_Out, multiplexer_1_out, Opcode_tun, register_file_1_data_outb;
  wire [7:0] counter_Out_tun;
  wire [11:3] Program_Decoder_data;

  Clock clk (.out(clk_tun));
  Counter Binary_Counter (
    .clr(Reset), .load(1'b0), .up(1'b1), .count(1'b1), .clk(clk_tun), .Q(counter_Out_tun));  // open: D, carry
  ROM #(.dataWidth(16)) Program_Decoder (
    .addr(counter_Out_tun),
    .data({Opcode_tun, Program_Decoder_data[11], addrD_tun, Program_Decoder_data[7], addrA_tun, Program_Decoder_data[3], Addr_B}));
  ROM #(.addrWidth(4), .dataWidth(7)) Instructions_Decoder (.addr(Opcode_tun), .data({SUB, AFS, RSS, DWE, WE}));
  // Probe on {Opcode_tun, Program_Decoder_data[11], addrD_tun, Program_Decoder_data[7], addrA_tun, Program_Decoder_data[3], Addr_B}
  // Probe on nothing
  // Probe on counter_Out_tun
  Multiplexer #(.select(2), .width(4)) multiplexer_1 (
    .in0({Program_Decoder_data[3], Addr_B}), .in1(ALU_Out), .in2(A_out), .out(multiplexer_1_out), .sel(RSS));  // open: in3
  TTY tty_1 (.data({A_out[2:0], register_file_1_data_outb}), .clk(clk_tun), .we(DWE), .clr(Reset));
  register_file register_file_1 (
    .WE(WE), .WAddr(addrD_tun), .RAddrA(addrA_tun), .RAddrB(Addr_B), .Data_in(multiplexer_1_out),
    .Clk(clk_tun), .Data_outA(A_out), .Data_outB(register_file_1_data_outb));
  // Probe on ALU_Out
  ALU_8 alu_8_1 (.A(A_out), .B(register_file_1_data_outb), .S({SUB, AFS}), .ALU_out(ALU_Out));

  // Other names for the same wires on the sheet: reset_tun = Reset

  // Notes on the sheet:
  //   contents of Program_Decoder (hex, n*v repeats v):
  //   1004 1109 1606 1701 120e 3001 3067 3062 1402 1500 3045 1005 1103 3001 1205 3062 3067 1007 1102 3001
  //   100c 3060 3062 3045 1003 3010 1003 1102 1207 3001 3002 100a 0 0 2640 2750 10*0 1300 3030 1600 170a
  //   1003 1404 3004 1102 120b 3012 1302 3001 110d 3001 7534 3005 0 3067 3004 1202 3027 3002 130d 3003
  //   7544 3005 7*0 3067 3004 110d 3021 3002 3001 130f 4523 1301 7553 7554 3005 4*0 3067 3004 110b 3021
  //   3002 110d 3001 7542 3005 7*0 3067 128*0 3004 110d 3021 3002 3001 f542 3005 8*0 3067
  //   contents of Instructions_Decoder (hex, n*v repeats v):
  //   0 1 9 2 5 15 25 35 7*0 75
endmodule

module Four_bit_register (
  input  [3:0] Din,
  input  Write_EN,
  input  Clk,
  output [3:0] Dout
);

  wire [3:0] multiplexer_1_out;

  Multiplexer #(.width(4)) multiplexer_1 (.in0(Dout), .in1(Din), .out(multiplexer_1_out), .sel(Write_EN));
  D_Flip_Flop d_ff_1 (.D(multiplexer_1_out[0]), .clk(Clk), .Q(Dout[0]));  // open: Qn, preset, reset
  D_Flip_Flop d_ff_2 (.D(multiplexer_1_out[1]), .clk(Clk), .Q(Dout[1]));  // open: Qn, preset, reset
  D_Flip_Flop d_ff_3 (.D(multiplexer_1_out[2]), .clk(Clk), .Q(Dout[2]));  // open: Qn, preset, reset
  D_Flip_Flop d_ff_4 (.D(multiplexer_1_out[3]), .clk(Clk), .Q(Dout[3]));  // open: Qn, preset, reset

  // Notes on the sheet:
  //   Ian J. Searle
endmodule

module register_file (
  input  WE,
  input  [2:0] WAddr,
  input  [2:0] RAddrA,
  input  [2:0] RAddrB,
  input  [3:0] Data_in,
  input  Clk,
  output [3:0] Data_outA,
  output [3:0] Data_outB
);

  wire decoder_1_out0, decoder_1_out1, decoder_1_out2, decoder_1_out3, decoder_1_out4, decoder_1_out5,
       decoder_1_out6, decoder_1_out7;
  wire [3:0] Dout_0, Dout_1, Dout_2, Dout_3, Dout_4, Dout_5, Dout_6, Dout_7;

  Decoder #(.select(3)) decoder_1 (
    .out0(decoder_1_out0), .out1(decoder_1_out1), .out2(decoder_1_out2), .out3(decoder_1_out3),
    .out4(decoder_1_out4), .out5(decoder_1_out5), .out6(decoder_1_out6), .out7(decoder_1_out7), .sel(WAddr),
    .en(WE));
  Four_bit_register four_bit_register_1 (.Din(Data_in), .Write_EN(decoder_1_out0), .Clk(Clk), .Dout(Dout_0));
  Four_bit_register four_bit_register_2 (.Din(Data_in), .Write_EN(decoder_1_out1), .Clk(Clk), .Dout(Dout_1));
  Four_bit_register four_bit_register_3 (.Din(Data_in), .Write_EN(decoder_1_out2), .Clk(Clk), .Dout(Dout_2));
  Four_bit_register four_bit_register_4 (.Din(Data_in), .Write_EN(decoder_1_out3), .Clk(Clk), .Dout(Dout_3));
  Four_bit_register four_bit_register_5 (.Din(Data_in), .Write_EN(decoder_1_out4), .Clk(Clk), .Dout(Dout_4));
  Four_bit_register four_bit_register_6 (.Din(Data_in), .Write_EN(decoder_1_out5), .Clk(Clk), .Dout(Dout_5));
  Four_bit_register four_bit_register_7 (.Din(Data_in), .Write_EN(decoder_1_out6), .Clk(Clk), .Dout(Dout_6));
  Four_bit_register four_bit_register_8 (.Din(Data_in), .Write_EN(decoder_1_out7), .Clk(Clk), .Dout(Dout_7));
  Multiplexer #(.select(3), .width(4)) multiplexer_1 (
    .in0(Dout_0), .in1(Dout_1), .in2(Dout_2), .in3(Dout_3), .in4(Dout_4), .in5(Dout_5), .in6(Dout_6),
    .in7(Dout_7), .out(Data_outA), .sel(RAddrA));
  Multiplexer #(.select(3), .width(4)) multiplexer_2 (
    .in0(Dout_0), .in1(Dout_1), .in2(Dout_2), .in3(Dout_3), .in4(Dout_4), .in5(Dout_5), .in6(Dout_6),
    .in7(Dout_7), .out(Data_outB), .sel(RAddrB));

  // Notes on the sheet:
  //   Ian J Searle
endmodule

module ALU_8 (
  input  [3:0] A,
  input  [3:0] B,
  input  [2:0] S,
  output [3:0] ALU_out
);

  wire [3:0] add_4bit_1_add4, and_4bit_1_and4, compliment_1_com_out, or_4bit_1_or4, shift_left_1_out_2,
       shift_right_1_out_2, xor_4bit_1_xor4;

  XOR_4bit xor_4bit_1 (.A(A), .B(B), .XOR4(xor_4bit_1_xor4));
  AND_4bit and_4bit_1 (.A(A), .B(B), .AND4(and_4bit_1_and4));
  OR_4bit or_4bit_1 (.A(A), .B(B), .OR4(or_4bit_1_or4));
  Add_4bit add_4bit_1 (.SUB(S[2]), .A(A), .B(B), .ADD4(add_4bit_1_add4));
  SHIFT_RIGHT shift_right_1 (.A(A), .out_2(shift_right_1_out_2));
  Compliment compliment_1 (.In_0(A), .Com_out(compliment_1_com_out));
  Shift_Left shift_left_1 (.A(A), .out_2(shift_left_1_out_2));
  Add_4bit add_4bit_2 (.A(A), .B(B));  // open: SUB, ADD4
  MUX8_1 mux8_1_1 (
    .M1_0(xor_4bit_1_xor4), .M1_1(and_4bit_1_and4), .M1_2(or_4bit_1_or4), .M1_3(add_4bit_1_add4),
    .M2_0(shift_right_1_out_2), .M2_1(compliment_1_com_out), .M2_2(shift_left_1_out_2),
    .M2_3(add_4bit_1_add4), .S(S), .MUX6_1_OUT(ALU_out));

  // Notes on the sheet:
  //   Ian J Searle
endmodule

module MUX2to1_1bit (
  input  A,
  input  S,
  input  B,
  output F
);

  wire and_1_out, and_2_out, not_1_out;

  not not_1 (not_1_out, S);
  and and_1 (and_1_out, A, not_1_out);
  and and_2 (and_2_out, S, B);
  or or_1 (F, and_1_out, and_2_out);
endmodule

module MUX2to1_4bit (
  input  [3:0] A,
  input  S,
  input  [3:0] B,
  output [3:0] F
);

  MUX2to1_1bit mux2to1_1bit_1 (.A(A[3]), .S(S), .B(B[3]), .F(F[3]));
  MUX2to1_1bit mux2to1_1bit_2 (.A(A[2]), .S(S), .B(B[2]), .F(F[2]));
  MUX2to1_1bit mux2to1_1bit_3 (.A(A[1]), .S(S), .B(B[1]), .F(F[1]));
  MUX2to1_1bit mux2to1_1bit_4 (.A(A[0]), .S(S), .B(B[0]), .F(F[0]));
endmodule

module Full_Adder (
  input  A,
  input  B,
  input  Cin,
  output S,
  output Cout
);

  wire and_1_out, and_2_out, and_3_out, xor_1_out;

  and and_1 (and_1_out, B, Cin);
  and and_2 (and_2_out, B, A);
  and and_3 (and_3_out, A, Cin);
  xor xor_1 (xor_1_out, B, Cin);
  xor xor_2 (S, A, xor_1_out);
  or or_1 (Cout, and_1_out, and_2_out, and_3_out);
endmodule

module AND_4bit (
  input  [3:0] A,
  input  [3:0] B,
  output [3:0] AND4
);

  and and_1 (AND4[3], A[3], B[3]);
  and and_2 (AND4[2], A[2], B[2]);
  and and_3 (AND4[1], A[1], B[1]);
  and and_4 (AND4[0], A[0], B[0]);
endmodule

module OR_4bit (
  input  [3:0] A,
  input  [3:0] B,
  output [3:0] OR4
);

  or or_1 (OR4[3], A[3], B[3]);
  or or_2 (OR4[2], A[2], B[2]);
  // Probe on OR4[3]
  or or_3 (OR4[1], A[1], B[1]);
  or or_4 (OR4[0], A[0], B[0]);
endmodule

module XOR_4bit (
  input  [3:0] A,
  input  [3:0] B,
  output [3:0] XOR4
);

  xor xor_1 (XOR4[3], A[3], B[3]);
  xor xor_2 (XOR4[2], A[2], B[2]);
  xor xor_3 (XOR4[1], A[1], B[1]);
  xor xor_4 (XOR4[0], A[0], B[0]);

  // Notes on the sheet:
  //   Ian J. Searle
endmodule

module MUX4to1_4bit (
  input  [3:0] IN0,
  input  [3:0] IN2,
  input  [3:0] IN1,
  input  [3:0] IN3,
  input  [1:0] S,
  output [3:0] MUX_out
);

  wire [3:0] mux2to1_4bit_1_f, mux2to1_4bit_2_f;

  MUX2to1_4bit mux2to1_4bit_1 (.A(IN0), .S(S[1]), .B(IN2), .F(mux2to1_4bit_1_f));
  MUX2to1_4bit mux2to1_4bit_2 (.A(IN1), .S(S[1]), .B(IN3), .F(mux2to1_4bit_2_f));
  MUX2to1_4bit mux2to1_4bit_3 (.A(mux2to1_4bit_1_f), .S(S[0]), .B(mux2to1_4bit_2_f), .F(MUX_out));

  // Notes on the sheet:
  //   (A input)
  //   (C input)
  //   (B input)
  //   (D input)
  //   (F)
endmodule

module Add_4bit (
  input  SUB,
  input  [3:0] A,
  input  [3:0] B,
  output [3:0] ADD4
);

  wire full_adder_1_cout, full_adder_2_cout, full_adder_3_cout, xor_1_out, xor_2_out, xor_3_out, xor_4_out;

  xor xor_1 (xor_1_out, B[0], SUB);
  xor xor_2 (xor_2_out, B[1], SUB);
  xor xor_3 (xor_3_out, B[2], SUB);
  xor xor_4 (xor_4_out, B[3], SUB);
  Full_Adder full_adder_1 (.A(A[0]), .B(xor_1_out), .Cin(SUB), .S(ADD4[0]), .Cout(full_adder_1_cout));
  Full_Adder full_adder_2 (.A(A[1]), .B(xor_2_out), .Cin(full_adder_1_cout), .S(ADD4[1]), .Cout(full_adder_2_cout));
  Full_Adder full_adder_3 (.A(A[2]), .B(xor_3_out), .Cin(full_adder_2_cout), .S(ADD4[2]), .Cout(full_adder_3_cout));
  Full_Adder full_adder_4 (.A(A[3]), .B(xor_4_out), .Cin(full_adder_3_cout), .S(ADD4[3]));  // open: Cout

  // Notes on the sheet:
  //   Ian J Searle
endmodule

module SHIFT_RIGHT (
  input  [3:0] A,
  output [3:0] out_2
);


  assign out_2 = {A[2:0], 1'b0};

  // Notes on the sheet:
  //   Ian Searle
endmodule

module Shift_Left (
  input  [3:0] A,
  output [3:0] out_2
);


  assign out_2 = {1'b0, A[3:1]};

  // Notes on the sheet:
  //   Ian Searle
endmodule

module MUX8_1 (
  input  [3:0] M1_0,
  input  [3:0] M1_1,
  input  [3:0] M1_2,
  input  [3:0] M1_3,
  input  [3:0] M2_0,
  input  [3:0] M2_1,
  input  [3:0] M2_2,
  input  [3:0] M2_3,
  input  [2:0] S,
  output [3:0] MUX6_1_OUT
);

  wire [3:0] mux4to1_4bit_1_mux_out, mux4to1_4bit_2_mux_out;

  MUX4to1_4bit mux4to1_4bit_1 (
    .IN0(M1_0), .IN2(M1_1), .IN1(M1_2), .IN3(M1_3), .S(S[1:0]), .MUX_out(mux4to1_4bit_1_mux_out));
  MUX4to1_4bit mux4to1_4bit_2 (
    .IN0(M2_0), .IN2(M2_1), .IN1(M2_2), .IN3(M2_3), .S(S[1:0]), .MUX_out(mux4to1_4bit_2_mux_out));
  MUX2to1_4bit mux2to1_4bit_1 (.A(mux4to1_4bit_1_mux_out), .S(S[2]), .B(mux4to1_4bit_2_mux_out), .F(MUX6_1_OUT));

  // Notes on the sheet:
  //   Ian Searle
endmodule

module Compliment (
  input  [3:0] In_0,
  output [3:0] Com_out
);

  not not_1 (Com_out[0], In_0[0]);
  not not_2 (Com_out[1], In_0[1]);
  not not_3 (Com_out[2], In_0[2]);
  not not_4 (Com_out[3], In_0[3]);

  // Notes on the sheet:
  //   Ian J. Searle
endmodule

module Subtrac (
  input  [3:0] A,
  input  [3:0] B,
  output [3:0] Sub_out
);

  wire [3:0] compliment_1_com_out;

  Compliment compliment_1 (.In_0(B), .Com_out(compliment_1_com_out));
  Add_4bit add_4bit_1 (.SUB(1'b1), .A(A), .B(compliment_1_com_out), .ADD4(Sub_out));

  // Notes on the sheet:
  //   Ian
endmodule
