// Logisim project Register_File.circ as structural Verilog: 2 circuits, main circuit register_file
module register_file (
  input  WE,
  input  [2:0] WAddr,
  input  [2:0] RAddr,
  input  [3:0] Data_in,
  input  Clk,
  output [3:0] Data_out
);

  wire decoder_1_out0, decoder_1_out1, decoder_1_out2, decoder_1_out3, decoder_1_out4, decoder_1_out5,
       decoder_1_out6, decoder_1_out7;
  wire [3:0] four_bit_register_1_dout, four_bit_register_2_dout, four_bit_register_3_dout,
       four_bit_register_4_dout, four_bit_register_5_dout, four_bit_register_6_dout,
       four_bit_register_7_dout, four_bit_register_8_dout;

  Decoder #(.select(3)) decoder_1 (
    .out0(decoder_1_out0), .out1(decoder_1_out1), .out2(decoder_1_out2), .out3(decoder_1_out3),
    .out4(decoder_1_out4), .out5(decoder_1_out5), .out6(decoder_1_out6), .out7(decoder_1_out7), .sel(WAddr),
    .en(WE));
  Four_bit_register four_bit_register_1 (
    .Din(Data_in), .Write_EN(decoder_1_out0), .Clk(Clk), .Dout(four_bit_register_1_dout));
  Four_bit_register four_bit_register_2 (
    .Din(Data_in), .Write_EN(decoder_1_out1), .Clk(Clk), .Dout(four_bit_register_2_dout));
  Four_bit_register four_bit_register_3 (
    .Din(Data_in), .Write_EN(decoder_1_out2), .Clk(Clk), .Dout(four_bit_register_3_dout));
  Four_bit_register four_bit_register_4 (
    .Din(Data_in), .Write_EN(decoder_1_out3), .Clk(Clk), .Dout(four_bit_register_4_dout));
  Four_bit_register four_bit_register_5 (
    .Din(Data_in), .Write_EN(decoder_1_out4), .Clk(Clk), .Dout(four_bit_register_5_dout));
  Four_bit_register four_bit_register_6 (
    .Din(Data_in), .Write_EN(decoder_1_out5), .Clk(Clk), .Dout(four_bit_register_6_dout));
  Four_bit_register four_bit_register_7 (
    .Din(Data_in), .Write_EN(decoder_1_out6), .Clk(Clk), .Dout(four_bit_register_7_dout));
  Four_bit_register four_bit_register_8 (
    .Din(Data_in), .Write_EN(decoder_1_out7), .Clk(Clk), .Dout(four_bit_register_8_dout));
  Multiplexer #(.select(3), .width(4)) multiplexer_1 (
    .in0(four_bit_register_1_dout), .in1(four_bit_register_2_dout), .in2(four_bit_register_3_dout),
    .in3(four_bit_register_4_dout), .in4(four_bit_register_5_dout), .in5(four_bit_register_6_dout),
    .in6(four_bit_register_7_dout), .in7(four_bit_register_8_dout), .out(Data_out), .sel(RAddr));

  // Notes on the sheet:
  //   Ian J Searle
endmodule

module Four_bit_register (
  input  [3:0] Din,
  input  Write_EN,
  input  Clk,
  output [3:0] Dout
);

  wire [3:0] multiplexer_1_out;

  Multiplexer #(.width(4)) multiplexer_1 (.in0(Dout), .in1(Din), .out(multiplexer_1_out), .sel(Write_EN));
  D_Flip_Flop d_ff_1 (.D(multiplexer_1_out[0]), .clk(Clk), .Q(Dout[0]));  // open: Qn, preset, reset
  D_Flip_Flop d_ff_2 (.D(multiplexer_1_out[1]), .clk(Clk), .Q(Dout[1]));  // open: Qn, preset, reset
  D_Flip_Flop d_ff_3 (.D(multiplexer_1_out[2]), .clk(Clk), .Q(Dout[2]));  // open: Qn, preset, reset
  D_Flip_Flop d_ff_4 (.D(multiplexer_1_out[3]), .clk(Clk), .Q(Dout[3]));  // open: Qn, preset, reset

  // Notes on the sheet:
  //   Ian J. Searle
endmodule
